// Logisim project TOY-8 CPU_WS.circ as structural Verilog: 25 circuits, main circuit Interface
module Interface (
  input  [3:0] Address,
  input  [7:0] Data,
  output [3:0] out_3,
  output [7:0] out_4,
  output [7:0] out_5,
  output [7:0] out_6,
  output [7:0] out_7,
  output [7:0] out_8,
  output [7:0] out_9,
  output [7:0] out_10,
  output [7:0] out_11,
  output [7:0] out_12,
  output [7:0] out_13,
  output [7:0] out_14,
  output [7:0] out_15,
  output [7:0] out_16,
  output [7:0] out_17,
  output [7:0] out_18,
  output [7:0] out_19
);

  wire clock_1_out, cpu_1_running, LOAD_out, RUN_out;

  Button RUN (.out(RUN_out));
  Button LOAD (.out(LOAD_out));
  LedBar ledbar_1 (
    .led0(Data[7]), .led1(Data[6]), .led2(Data[5]), .led3(Data[4]), .led4(Data[3]), .led5(Data[2]),
    .led6(Data[1]), .led7(Data[0]));
  LedBar #(.matrixcols(4)) ledbar_2 (.led0(Address[3]), .led1(Address[2]), .led2(Address[1]), .led3(Address[0]));
  Clock clock_1 (.out(clock_1_out));
  LED Active (.in(cpu_1_running));
  CPU cpu_1 (
    .Clk(clock_1_out), .Run(RUN_out), .Load(LOAD_out), .Addr(Address), .Data(Data), .Running(cpu_1_running),
    .PC(out_3), .x0(out_4), .x1(out_5), .x2(out_6), .x3(out_7), .x4(out_8), .x5(out_9), .x6(out_10),
    .x7(out_11), .x8(out_12), .x9(out_13), .xA(out_14), .xB(out_15), .xC(out_16), .xD(out_17), .xE(out_18),
    .xF(out_19));

  // Notes on the sheet:
  //   Make Sure Address and Data are set
  //   to 0 when running program
  //   Data
  //   Address
  //   In Binary
endmodule

module CPU (
  input  Clk,
  input  Run,
  input  Load,
  input  [3:0] Addr,
  input  [7:0] Data,
  output Running,
  output [3:0] PC,
  output [7:0] x0,
  output [7:0] x1,
  output [7:0] x2,
  output [7:0] x3,
  output [7:0] x4,
  output [7:0] x5,
  output [7:0] x6,
  output [7:0] x7,
  output [7:0] x8,
  output [7:0] x9,
  output [7:0] xA,
  output [7:0] xB,
  output [7:0] xC,
  output [7:0] xD,
  output [7:0] xE,
  output [7:0] xF
);

  wire clock_circuit_1_execute, clock_circuit_1_execute_write, clock_circuit_1_fetch,
       clock_circuit_1_fetch_write, control_circuit_1_addr_mux_ir, control_circuit_1_addr_mux_pc,
       control_circuit_1_alu_add, control_circuit_1_alu_and, control_circuit_1_alu_ls,
       control_circuit_1_alu_rs, control_circuit_1_alu_xor, control_circuit_1_halt,
       control_circuit_1_ir_write, control_circuit_1_memory_write, control_circuit_1_pc_increment,
       control_circuit_1_pc_load, control_circuit_1_pc_write, control_circuit_1_r_mux_alu,
       control_circuit_1_r_mux_ir, control_circuit_1_r_mux_memory, control_circuit_1_r_write, or_2_out;
  wire [3:0] ir_1_o, or_3_out, two_way_bus_mux_1_o;
  wire [7:0] alu_1_o, memory_bank_1_o, or_1_out, r_mux_three_way_1_o, register_8_bit_1_o;
  wire [7:4] ir_1_o_2;

  ALU alu_1 (
    .A(register_8_bit_1_o), .B(memory_bank_1_o), .ALU_ADD(control_circuit_1_alu_add),
    .ALU_AND(control_circuit_1_alu_and), .ALU_XOR(control_circuit_1_alu_xor),
    .ALU_LS(control_circuit_1_alu_ls), .ALU_RS(control_circuit_1_alu_rs), .O(alu_1_o));
  R_MUX_Three_Way r_mux_three_way_1 (
    .ALU(alu_1_o), .Mem(memory_bank_1_o), .IR(ir_1_o), .R_MUX_ALU(control_circuit_1_r_mux_alu),
    .R_MUX_Mem(control_circuit_1_r_mux_memory), .R_MUX_IR(control_circuit_1_r_mux_ir), .O(r_mux_three_way_1_o));
  Register_8_Bit register_8_bit_1 (.I(r_mux_three_way_1_o), .WE(control_circuit_1_r_write), .O(register_8_bit_1_o));
  IR ir_1 (.I(memory_bank_1_o), .WE(control_circuit_1_ir_write), .O({ir_1_o_2, ir_1_o}));
  Clock_Circuit clock_circuit_1 (
    .Clk(Clk), .Run(Run), .Halt(control_circuit_1_halt), .Running(Running), .Fetch(clock_circuit_1_fetch),
    .Fetch_Write(clock_circuit_1_fetch_write), .Execute(clock_circuit_1_execute),
    .Execute_Write(clock_circuit_1_execute_write));
  Control_Circuit control_circuit_1 (
    .Fetch(clock_circuit_1_fetch), .Fetch_Write(clock_circuit_1_fetch_write),
    .Execute(clock_circuit_1_execute), .Execute_Write(clock_circuit_1_execute_write), .Opcode(ir_1_o_2),
    .R(register_8_bit_1_o), .Halt(control_circuit_1_halt), .ALU_Add(control_circuit_1_alu_add),
    .ALU_AND(control_circuit_1_alu_and), .ALU_XOR(control_circuit_1_alu_xor),
    .Memory_Write(control_circuit_1_memory_write), .ALU_LS(control_circuit_1_alu_ls),
    .ALU_RS(control_circuit_1_alu_rs), .PC_Increment(control_circuit_1_pc_increment),
    .R_MUX_ALU(control_circuit_1_r_mux_alu), .PC_Load(control_circuit_1_pc_load),
    .R_MUX_Memory(control_circuit_1_r_mux_memory), .R_MUX_IR(control_circuit_1_r_mux_ir),
    .PC_Write(control_circuit_1_pc_write), .ADDR_MUX_PC(control_circuit_1_addr_mux_pc),
    .ADDR_MUX_IR(control_circuit_1_addr_mux_ir), .R_Write(control_circuit_1_r_write),
    .IR_Write(control_circuit_1_ir_write));
  assign or_1_out = Data | register_8_bit_1_o;  // OR_Gate or_1, 8 bits wide
  PC_Circuit pc_circuit_1 (
    .I(ir_1_o), .PC_Increment(control_circuit_1_pc_increment), .PC_Load(control_circuit_1_pc_load),
    .PC_Write(control_circuit_1_pc_write), .O(PC));
  Two_Way_Bus_Mux two_way_bus_mux_1 (
    .I1(PC), .I2(ir_1_o), .E1(control_circuit_1_addr_mux_pc), .E2(control_circuit_1_addr_mux_ir),
    .O(two_way_bus_mux_1_o));
  or or_2 (or_2_out, Load, control_circuit_1_memory_write);
  assign or_3_out = two_way_bus_mux_1_o | Addr;  // OR_Gate or_3, 4 bits wide
  Memory_Bank memory_bank_1 (
    .I(or_1_out), .Addr(or_3_out), .WE(or_2_out), .x0(x0), .x1(x1), .x2(x2), .x3(x3), .x4(x4), .x5(x5),
    .x6(x6), .x7(x7), .x8(x8), .x9(x9), .xA(xA), .xB(xB), .xC(xC), .xD(xD), .xE(xE), .xF(xF),
    .O(memory_bank_1_o));
endmodule

module MAJ (
  input  A,
  input  B,
  input  C,
  output O
);

  wire and_1_out, and_2_out, and_3_out;

  and and_1 (and_1_out, A, B);
  and and_2 (and_2_out, A, C);
  and and_3 (and_3_out, B, C);
  or or_1 (O, and_1_out, and_2_out, and_3_out);
endmodule

module ODD (
  input  A,
  input  B,
  input  C,
  output O
);

  wire and_1_out, xor_1_out;

  ExactlyOne xor_1 (.out(xor_1_out), .in0(A), .in1(B), .in2(C));
  and and_1 (and_1_out, C, B, A);
  or or_1 (O, xor_1_out, and_1_out);
endmodule

module Adder_8_Bit (
  input  [7:0] A,
  input  [7:0] B,
  output [7:0] O
);

  wire maj_1_o, maj_2_o, maj_3_o, maj_4_o, maj_5_o, maj_6_o, maj_7_o;

  MAJ maj_1 (.A(A[0]), .B(B[0]), .C(1'b0), .O(maj_1_o));
  ODD odd_1 (.A(A[0]), .B(B[0]), .C(1'b0), .O(O[0]));
  MAJ maj_2 (.A(A[1]), .B(B[1]), .C(maj_1_o), .O(maj_2_o));
  ODD odd_2 (.A(A[1]), .B(B[1]), .C(maj_1_o), .O(O[1]));
  MAJ maj_3 (.A(A[2]), .B(B[2]), .C(maj_2_o), .O(maj_3_o));
  ODD odd_3 (.A(A[2]), .B(B[2]), .C(maj_2_o), .O(O[2]));
  MAJ maj_4 (.A(A[3]), .B(B[3]), .C(maj_3_o), .O(maj_4_o));
  ODD odd_4 (.A(A[3]), .B(B[3]), .C(maj_3_o), .O(O[3]));
  MAJ maj_5 (.A(A[4]), .B(B[4]), .C(maj_4_o), .O(maj_5_o));
  ODD odd_5 (.A(A[4]), .B(B[4]), .C(maj_4_o), .O(O[4]));
  MAJ maj_6 (.A(A[5]), .B(B[5]), .C(maj_5_o), .O(maj_6_o));
  ODD odd_6 (.A(A[5]), .B(B[5]), .C(maj_5_o), .O(O[5]));
  MAJ maj_7 (.A(A[6]), .B(B[6]), .C(maj_6_o), .O(maj_7_o));
  ODD odd_7 (.A(A[6]), .B(B[6]), .C(maj_6_o), .O(O[6]));
  MAJ maj_8 (.A(A[7]), .B(B[7]), .C(maj_7_o));  // open: O
  ODD odd_8 (.A(A[7]), .B(B[7]), .C(maj_7_o), .O(O[7]));
endmodule

module Decoder_4_16 (
  input  [3:0] in_1,
  output out_2,
  output out_3,
  output out_4,
  output out_5,
  output out_6,
  output out_7,
  output out_8,
  output out_9,
  output out_10,
  output out_11,
  output out_12,
  output out_13,
  output out_14,
  output out_15,
  output out_16,
  output out_17
);

  and and_1 (out_2, ~in_1[0], ~in_1[1], ~in_1[2], ~in_1[3]);  // AND_Gate
  and and_2 (out_3, in_1[0], ~in_1[1], ~in_1[2], ~in_1[3]);  // AND_Gate
  and and_3 (out_4, ~in_1[0], in_1[1], ~in_1[2], ~in_1[3]);  // AND_Gate
  and and_4 (out_5, in_1[0], in_1[1], ~in_1[2], ~in_1[3]);  // AND_Gate
  and and_5 (out_6, ~in_1[0], ~in_1[1], in_1[2], ~in_1[3]);  // AND_Gate
  and and_6 (out_7, in_1[0], ~in_1[1], in_1[2], ~in_1[3]);  // AND_Gate
  and and_7 (out_8, ~in_1[0], in_1[1], in_1[2], ~in_1[3]);  // AND_Gate
  and and_8 (out_9, in_1[0], in_1[1], in_1[2], ~in_1[3]);  // AND_Gate
  and and_9 (out_10, ~in_1[0], ~in_1[1], ~in_1[2], in_1[3]);  // AND_Gate
  and and_10 (out_11, in_1[0], ~in_1[1], ~in_1[2], in_1[3]);  // AND_Gate
  and and_11 (out_12, ~in_1[0], in_1[1], ~in_1[2], in_1[3]);  // AND_Gate
  and and_12 (out_13, in_1[0], in_1[1], ~in_1[2], in_1[3]);  // AND_Gate
  and and_13 (out_14, ~in_1[0], ~in_1[1], in_1[2], in_1[3]);  // AND_Gate
  and and_14 (out_15, in_1[0], ~in_1[1], in_1[2], in_1[3]);  // AND_Gate
  and and_15 (out_16, ~in_1[0], in_1[1], in_1[2], in_1[3]);  // AND_Gate
  and and_16 (out_17, in_1[0], in_1[1], in_1[2], in_1[3]);
endmodule

module Demux_4_16 (
  input  [3:0] I,
  input  E,
  output out_3,
  output out_4,
  output out_5,
  output out_6,
  output out_7,
  output out_8,
  output out_9,
  output out_10,
  output out_11,
  output out_12,
  output out_13,
  output out_14,
  output out_15,
  output out_16,
  output out_17,
  output out_18
);

  wire and_1_out, and_2_out, and_3_out, and_4_out, and_5_out, and_6_out, and_7_out, and_8_out, and_9_out,
       and_10_out, and_11_out, and_12_out, and_13_out, and_14_out, and_15_out, and_16_out;

  and and_1 (and_1_out, ~I[0], ~I[1], ~I[2], ~I[3]);  // AND_Gate
  and and_2 (and_2_out, I[0], ~I[1], ~I[2], ~I[3]);  // AND_Gate
  and and_3 (and_3_out, ~I[0], I[1], ~I[2], ~I[3]);  // AND_Gate
  and and_4 (and_4_out, I[0], I[1], ~I[2], ~I[3]);  // AND_Gate
  and and_5 (and_5_out, ~I[0], ~I[1], I[2], ~I[3]);  // AND_Gate
  and and_6 (and_6_out, I[0], ~I[1], I[2], ~I[3]);  // AND_Gate
  and and_7 (and_7_out, ~I[0], I[1], I[2], ~I[3]);  // AND_Gate
  and and_8 (and_8_out, I[0], I[1], I[2], ~I[3]);  // AND_Gate
  and and_9 (and_9_out, ~I[0], ~I[1], ~I[2], I[3]);  // AND_Gate
  and and_10 (and_10_out, I[0], ~I[1], ~I[2], I[3]);  // AND_Gate
  and and_11 (and_11_out, ~I[0], I[1], ~I[2], I[3]);  // AND_Gate
  and and_12 (and_12_out, I[0], I[1], ~I[2], I[3]);  // AND_Gate
  and and_13 (and_13_out, ~I[0], ~I[1], I[2], I[3]);  // AND_Gate
  and and_14 (and_14_out, I[0], ~I[1], I[2], I[3]);  // AND_Gate
  and and_15 (and_15_out, ~I[0], I[1], I[2], I[3]);  // AND_Gate
  and and_16 (and_16_out, I[0], I[1], I[2], I[3]);
  and and_17 (out_3, and_1_out, E);
  and and_18 (out_4, and_2_out, E);
  and and_19 (out_5, and_3_out, E);
  and and_20 (out_6, and_4_out, E);
  and and_21 (out_7, and_5_out, E);
  and and_22 (out_8, and_6_out, E);
  and and_23 (out_9, and_7_out, E);
  and and_24 (out_10, and_8_out, E);
  and and_25 (out_11, and_9_out, E);
  and and_26 (out_12, and_10_out, E);
  and and_27 (out_13, and_11_out, E);
  and and_28 (out_14, and_12_out, E);
  and and_29 (out_15, and_13_out, E);
  and and_30 (out_16, and_14_out, E);
  and and_31 (out_17, and_15_out, E);
  and and_32 (out_18, and_16_out, E);
endmodule

module Bitwise_AND (
  input  [7:0] A,
  input  [7:0] B,
  output [7:0] O
);

  and and_1 (O[0], B[0], A[0]);
  and and_2 (O[1], B[1], A[1]);
  and and_3 (O[2], B[2], A[2]);
  and and_4 (O[3], B[3], A[3]);
  and and_5 (O[4], B[4], A[4]);
  and and_6 (O[5], B[5], A[5]);
  and and_7 (O[6], B[6], A[6]);
  and and_8 (O[7], B[7], A[7]);
endmodule

module Bitwise_OR (
  input  [7:0] A,
  input  [7:0] B,
  output [7:0] O
);

  or or_1 (O[0], B[0], A[0]);
  or or_2 (O[1], B[1], A[1]);
  or or_3 (O[2], B[2], A[2]);
  or or_4 (O[3], B[3], A[3]);
  or or_5 (O[4], B[4], A[4]);
  or or_6 (O[5], B[5], A[5]);
  or or_7 (O[6], B[6], A[6]);
  or or_8 (O[7], B[7], A[7]);
endmodule

module Bitwise_XOR (
  input  [7:0] A,
  input  [7:0] B,
  output [7:0] O
);

  xor xor_1 (O[0], B[0], A[0]);
  xor xor_2 (O[1], B[1], A[1]);
  xor xor_3 (O[2], B[2], A[2]);
  xor xor_4 (O[3], B[3], A[3]);
  xor xor_5 (O[4], B[4], A[4]);
  xor xor_6 (O[5], B[5], A[5]);
  xor xor_7 (O[6], B[6], A[6]);
  xor xor_8 (O[7], B[7], A[7]);
endmodule

module Left_Shift (
  input  [7:0] I,
  output [7:0] O
);


  assign O = {I[6:0], 1'b0};
endmodule

module Right_Shift (
  input  [7:0] I,
  output [7:0] O
);


  assign O = {1'b0, I[7:1]};
endmodule

module Enable_Line (
  input  [7:0] I,
  input  E,
  output [7:0] O
);

  and and_1 (O[0], I[0], E);
  and and_2 (O[1], I[1], E);
  and and_3 (O[2], I[2], E);
  and and_4 (O[3], I[3], E);
  and and_5 (O[4], I[4], E);
  and and_6 (O[5], I[5], E);
  and and_7 (O[6], I[6], E);
  and and_8 (O[7], I[7], E);
endmodule

module ALU (
  input  [7:0] A,
  input  [7:0] B,
  input  ALU_ADD,
  input  ALU_AND,
  input  ALU_XOR,
  input  ALU_LS,
  input  ALU_RS,
  output [7:0] O
);

  wire [7:0] adder_8_bit_1_o, bitwise_and_1_o, bitwise_or_1_o, bitwise_or_2_o, bitwise_or_3_o,
       bitwise_xor_1_o, enable_line_1_o, enable_line_2_o, enable_line_3_o, enable_line_4_o, enable_line_5_o,
       left_shift_1_o, right_shift_1_o;

  Adder_8_Bit adder_8_bit_1 (.A(A), .B(B), .O(adder_8_bit_1_o));
  Enable_Line enable_line_1 (.I(adder_8_bit_1_o), .E(ALU_ADD), .O(enable_line_1_o));
  Bitwise_AND bitwise_and_1 (.A(A), .B(B), .O(bitwise_and_1_o));
  Enable_Line enable_line_2 (.I(bitwise_and_1_o), .E(ALU_AND), .O(enable_line_2_o));
  Bitwise_OR bitwise_or_1 (.A(enable_line_2_o), .B(enable_line_1_o), .O(bitwise_or_1_o));
  Bitwise_XOR bitwise_xor_1 (.A(A), .B(B), .O(bitwise_xor_1_o));
  Enable_Line enable_line_3 (.I(bitwise_xor_1_o), .E(ALU_XOR), .O(enable_line_3_o));
  Bitwise_OR bitwise_or_2 (.A(enable_line_3_o), .B(bitwise_or_1_o), .O(bitwise_or_2_o));
  Left_Shift left_shift_1 (.I(A), .O(left_shift_1_o));
  Enable_Line enable_line_4 (.I(left_shift_1_o), .E(ALU_LS), .O(enable_line_4_o));
  Bitwise_OR bitwise_or_3 (.A(enable_line_4_o), .B(bitwise_or_2_o), .O(bitwise_or_3_o));
  Right_Shift right_shift_1 (.I(A), .O(right_shift_1_o));
  Enable_Line enable_line_5 (.I(right_shift_1_o), .E(ALU_RS), .O(enable_line_5_o));
  Bitwise_OR bitwise_or_4 (.A(enable_line_5_o), .B(bitwise_or_3_o), .O(O));
endmodule

module Clock_Circuit (
  input  Clk,
  input  Run,
  input  Halt,
  output Running,
  output Fetch,
  output Fetch_Write,
  output Execute,
  output Execute_Write
);

  wire and_3_out, and_4_out, and_5_out, not_1_out, or_1_out;

  and and_1 (Fetch_Write, and_5_out, Fetch);
  and and_2 (Execute_Write, and_5_out, Execute);
  not not_1 (not_1_out, Fetch);
  and and_3 (and_3_out, and_5_out, not_1_out);
  and and_4 (and_4_out, and_5_out, Fetch);
  not not_2 (Fetch, Execute);
  S_R_Flip_Flop #(.trigger("falling")) s_r_ff_1 (
    .S(and_4_out), .R(and_3_out), .clk(and_5_out), .Q(Execute));  // open: reset, Qn, preset
  and and_5 (and_5_out, Clk, Running);
  S_R_Flip_Flop s_r_ff_2 (.S(Run), .R(Halt), .clk(or_1_out), .Q(Running));  // open: reset, Qn, preset
  or or_1 (or_1_out, Run, Halt);
endmodule

module Memory_Cell (
  input  I,
  input  WE,
  output O
);

  wire and_1_out, and_2_out, clock_1_out, not_1_out;

  not not_1 (not_1_out, I);
  and and_1 (and_1_out, I, WE);
  and and_2 (and_2_out, not_1_out, WE);
  S_R_Flip_Flop #(.trigger("falling")) s_r_ff_1 (
    .S(and_1_out), .R(and_2_out), .clk(clock_1_out), .Q(O));  // open: reset, Qn, preset
  Clock clock_1 (.out(clock_1_out));
endmodule

module Register_8_Bit (
  input  [7:0] I,
  input  WE,
  output [7:0] O
);

  Memory_Cell memory_cell_1 (.I(I[0]), .WE(WE), .O(O[0]));
  Memory_Cell memory_cell_2 (.I(I[1]), .WE(WE), .O(O[1]));
  Memory_Cell memory_cell_3 (.I(I[2]), .WE(WE), .O(O[2]));
  Memory_Cell memory_cell_4 (.I(I[3]), .WE(WE), .O(O[3]));
  Memory_Cell memory_cell_5 (.I(I[4]), .WE(WE), .O(O[4]));
  Memory_Cell memory_cell_6 (.I(I[5]), .WE(WE), .O(O[5]));
  Memory_Cell memory_cell_7 (.I(I[6]), .WE(WE), .O(O[6]));
  Memory_Cell memory_cell_8 (.I(I[7]), .WE(WE), .O(O[7]));
endmodule

module IR (
  input  [7:0] I,
  input  WE,
  output [7:0] O
);

  Memory_Cell memory_cell_1 (.I(I[0]), .WE(WE), .O(O[0]));
  Memory_Cell memory_cell_2 (.I(I[1]), .WE(WE), .O(O[1]));
  Memory_Cell memory_cell_3 (.I(I[2]), .WE(WE), .O(O[2]));
  Memory_Cell memory_cell_4 (.I(I[3]), .WE(WE), .O(O[3]));
  Memory_Cell memory_cell_5 (.I(I[4]), .WE(WE), .O(O[4]));
  Memory_Cell memory_cell_6 (.I(I[5]), .WE(WE), .O(O[5]));
  Memory_Cell memory_cell_7 (.I(I[6]), .WE(WE), .O(O[6]));
  Memory_Cell memory_cell_8 (.I(I[7]), .WE(WE), .O(O[7]));
endmodule

module Memory_Bank (
  input  [7:0] I,
  input  [3:0] Addr,
  input  WE,
  output [7:0] x0,
  output [7:0] x1,
  output [7:0] x2,
  output [7:0] x3,
  output [7:0] x4,
  output [7:0] x5,
  output [7:0] x6,
  output [7:0] x7,
  output [7:0] x8,
  output [7:0] x9,
  output [7:0] xA,
  output [7:0] xB,
  output [7:0] xC,
  output [7:0] xD,
  output [7:0] xE,
  output [7:0] xF,
  output [7:0] O
);

  wire decoder_4_16_1_out_2, decoder_4_16_1_out_3, decoder_4_16_1_out_4, decoder_4_16_1_out_5,
       decoder_4_16_1_out_6, decoder_4_16_1_out_7, decoder_4_16_1_out_8, decoder_4_16_1_out_9,
       decoder_4_16_1_out_10, decoder_4_16_1_out_11, decoder_4_16_1_out_12, decoder_4_16_1_out_13,
       decoder_4_16_1_out_14, decoder_4_16_1_out_15, decoder_4_16_1_out_16, decoder_4_16_1_out_17,
       demux_4_16_1_out_3, demux_4_16_1_out_4, demux_4_16_1_out_5, demux_4_16_1_out_6, demux_4_16_1_out_7,
       demux_4_16_1_out_8, demux_4_16_1_out_9, demux_4_16_1_out_10, demux_4_16_1_out_11, demux_4_16_1_out_12,
       demux_4_16_1_out_13, demux_4_16_1_out_14, demux_4_16_1_out_15, demux_4_16_1_out_16,
       demux_4_16_1_out_17, demux_4_16_1_out_18;
  wire [7:0] bitwise_or_1_o, bitwise_or_2_o, bitwise_or_3_o, bitwise_or_4_o, bitwise_or_5_o, bitwise_or_6_o,
       bitwise_or_7_o, bitwise_or_8_o, bitwise_or_9_o, bitwise_or_10_o, bitwise_or_11_o, bitwise_or_12_o,
       bitwise_or_13_o, bitwise_or_14_o, enable_line_1_o, enable_line_2_o, enable_line_3_o, enable_line_4_o,
       enable_line_5_o, enable_line_6_o, enable_line_7_o, enable_line_8_o, enable_line_9_o, enable_line_10_o,
       enable_line_11_o, enable_line_12_o, enable_line_13_o, enable_line_14_o, enable_line_15_o,
       enable_line_16_o;

  Demux_4_16 demux_4_16_1 (
    .I(Addr), .E(WE), .out_3(demux_4_16_1_out_3), .out_4(demux_4_16_1_out_4), .out_5(demux_4_16_1_out_5),
    .out_6(demux_4_16_1_out_6), .out_7(demux_4_16_1_out_7), .out_8(demux_4_16_1_out_8),
    .out_9(demux_4_16_1_out_9), .out_10(demux_4_16_1_out_10), .out_11(demux_4_16_1_out_11),
    .out_12(demux_4_16_1_out_12), .out_13(demux_4_16_1_out_13), .out_14(demux_4_16_1_out_14),
    .out_15(demux_4_16_1_out_15), .out_16(demux_4_16_1_out_16), .out_17(demux_4_16_1_out_17),
    .out_18(demux_4_16_1_out_18));
  Decoder_4_16 decoder_4_16_1 (
    .in_1(Addr), .out_2(decoder_4_16_1_out_2), .out_3(decoder_4_16_1_out_3), .out_4(decoder_4_16_1_out_4),
    .out_5(decoder_4_16_1_out_5), .out_6(decoder_4_16_1_out_6), .out_7(decoder_4_16_1_out_7),
    .out_8(decoder_4_16_1_out_8), .out_9(decoder_4_16_1_out_9), .out_10(decoder_4_16_1_out_10),
    .out_11(decoder_4_16_1_out_11), .out_12(decoder_4_16_1_out_12), .out_13(decoder_4_16_1_out_13),
    .out_14(decoder_4_16_1_out_14), .out_15(decoder_4_16_1_out_15), .out_16(decoder_4_16_1_out_16),
    .out_17(decoder_4_16_1_out_17));
  Register_8_Bit register_8_bit_1 (.I(I), .WE(demux_4_16_1_out_3), .O(x0));
  Register_8_Bit register_8_bit_2 (.I(I), .WE(demux_4_16_1_out_4), .O(x1));
  Register_8_Bit register_8_bit_3 (.I(I), .WE(demux_4_16_1_out_5), .O(x2));
  Register_8_Bit register_8_bit_4 (.I(I), .WE(demux_4_16_1_out_6), .O(x3));
  Register_8_Bit register_8_bit_5 (.I(I), .WE(demux_4_16_1_out_7), .O(x4));
  Register_8_Bit register_8_bit_6 (.I(I), .WE(demux_4_16_1_out_8), .O(x5));
  Register_8_Bit register_8_bit_7 (.I(I), .WE(demux_4_16_1_out_9), .O(x6));
  Register_8_Bit register_8_bit_8 (.I(I), .WE(demux_4_16_1_out_10), .O(x7));
  Register_8_Bit register_8_bit_9 (.I(I), .WE(demux_4_16_1_out_11), .O(x8));
  Register_8_Bit register_8_bit_10 (.I(I), .WE(demux_4_16_1_out_12), .O(x9));
  Register_8_Bit register_8_bit_11 (.I(I), .WE(demux_4_16_1_out_13), .O(xA));
  Register_8_Bit register_8_bit_12 (.I(I), .WE(demux_4_16_1_out_14), .O(xB));
  Register_8_Bit register_8_bit_13 (.I(I), .WE(demux_4_16_1_out_15), .O(xC));
  Register_8_Bit register_8_bit_14 (.I(I), .WE(demux_4_16_1_out_16), .O(xD));
  Register_8_Bit register_8_bit_15 (.I(I), .WE(demux_4_16_1_out_17), .O(xE));
  Register_8_Bit register_8_bit_16 (.I(I), .WE(demux_4_16_1_out_18), .O(xF));
  Enable_Line enable_line_1 (.I(x0), .E(decoder_4_16_1_out_2), .O(enable_line_1_o));
  Enable_Line enable_line_2 (.I(x1), .E(decoder_4_16_1_out_3), .O(enable_line_2_o));
  Enable_Line enable_line_3 (.I(x2), .E(decoder_4_16_1_out_4), .O(enable_line_3_o));
  Enable_Line enable_line_4 (.I(x3), .E(decoder_4_16_1_out_5), .O(enable_line_4_o));
  Enable_Line enable_line_5 (.I(x4), .E(decoder_4_16_1_out_6), .O(enable_line_5_o));
  Enable_Line enable_line_6 (.I(x5), .E(decoder_4_16_1_out_7), .O(enable_line_6_o));
  Enable_Line enable_line_7 (.I(x6), .E(decoder_4_16_1_out_8), .O(enable_line_7_o));
  Enable_Line enable_line_8 (.I(x7), .E(decoder_4_16_1_out_9), .O(enable_line_8_o));
  Enable_Line enable_line_9 (.I(x8), .E(decoder_4_16_1_out_10), .O(enable_line_9_o));
  Enable_Line enable_line_10 (.I(x9), .E(decoder_4_16_1_out_11), .O(enable_line_10_o));
  Enable_Line enable_line_11 (.I(xA), .E(decoder_4_16_1_out_12), .O(enable_line_11_o));
  Enable_Line enable_line_12 (.I(xB), .E(decoder_4_16_1_out_13), .O(enable_line_12_o));
  Enable_Line enable_line_13 (.I(xC), .E(decoder_4_16_1_out_14), .O(enable_line_13_o));
  Enable_Line enable_line_14 (.I(xD), .E(decoder_4_16_1_out_15), .O(enable_line_14_o));
  Enable_Line enable_line_15 (.I(xE), .E(decoder_4_16_1_out_16), .O(enable_line_15_o));
  Enable_Line enable_line_16 (.I(xF), .E(decoder_4_16_1_out_17), .O(enable_line_16_o));
  Bitwise_OR bitwise_or_1 (.A(enable_line_1_o), .B(enable_line_2_o), .O(bitwise_or_1_o));
  Bitwise_OR bitwise_or_2 (.A(bitwise_or_1_o), .B(enable_line_3_o), .O(bitwise_or_2_o));
  Bitwise_OR bitwise_or_3 (.A(bitwise_or_2_o), .B(enable_line_4_o), .O(bitwise_or_3_o));
  Bitwise_OR bitwise_or_4 (.A(bitwise_or_3_o), .B(enable_line_5_o), .O(bitwise_or_4_o));
  Bitwise_OR bitwise_or_5 (.A(bitwise_or_4_o), .B(enable_line_6_o), .O(bitwise_or_5_o));
  Bitwise_OR bitwise_or_6 (.A(bitwise_or_5_o), .B(enable_line_7_o), .O(bitwise_or_6_o));
  Bitwise_OR bitwise_or_7 (.A(bitwise_or_6_o), .B(enable_line_8_o), .O(bitwise_or_7_o));
  Bitwise_OR bitwise_or_8 (.A(bitwise_or_7_o), .B(enable_line_9_o), .O(bitwise_or_8_o));
  Bitwise_OR bitwise_or_9 (.A(bitwise_or_8_o), .B(enable_line_10_o), .O(bitwise_or_9_o));
  Bitwise_OR bitwise_or_10 (.A(bitwise_or_9_o), .B(enable_line_11_o), .O(bitwise_or_10_o));
  Bitwise_OR bitwise_or_11 (.A(bitwise_or_10_o), .B(enable_line_12_o), .O(bitwise_or_11_o));
  Bitwise_OR bitwise_or_12 (.A(bitwise_or_11_o), .B(enable_line_13_o), .O(bitwise_or_12_o));
  Bitwise_OR bitwise_or_13 (.A(bitwise_or_12_o), .B(enable_line_14_o), .O(bitwise_or_13_o));
  Bitwise_OR bitwise_or_14 (.A(bitwise_or_13_o), .B(enable_line_15_o), .O(bitwise_or_14_o));
  Bitwise_OR bitwise_or_15 (.A(bitwise_or_14_o), .B(enable_line_16_o), .O(O));
endmodule

module Incrementer (
  input  [3:0] I,
  output [3:0] O
);

  wire and_2_out, and_3_out, and_4_out;

  // AND_Gate and_1 has open pins: in0=and_2_out, in1=I[3], out=open
  xor xor_1 (O[3], I[3], and_2_out);
  and and_2 (and_2_out, and_3_out, I[2]);
  xor xor_2 (O[2], I[2], and_3_out);
  and and_3 (and_3_out, and_4_out, I[1]);
  xor xor_3 (O[1], I[1], and_4_out);
  and and_4 (and_4_out, 1'b1, I[0]);
  xor xor_4 (O[0], I[0], 1'b1);
endmodule

module Two_Way_Bus_Mux (
  input  [3:0] I1,
  input  [3:0] I2,
  input  E1,
  input  E2,
  output [3:0] O
);

  wire and_1_out, and_2_out, and_3_out, and_4_out, and_5_out, and_6_out, and_7_out, and_8_out;

  and and_1 (and_1_out, E1, I1[0]);
  and and_2 (and_2_out, E2, I2[0]);
  xor xor_1 (O[0], and_1_out, and_2_out);
  and and_3 (and_3_out, E1, I1[1]);
  and and_4 (and_4_out, E2, I2[1]);
  xor xor_2 (O[1], and_3_out, and_4_out);
  and and_5 (and_5_out, E1, I1[2]);
  and and_6 (and_6_out, E2, I2[2]);
  xor xor_3 (O[2], and_5_out, and_6_out);
  and and_7 (and_7_out, E1, I1[3]);
  and and_8 (and_8_out, E2, I2[3]);
  xor xor_4 (O[3], and_7_out, and_8_out);
endmodule

module PC_Register (
  input  [3:0] I,
  input  E,
  output [3:0] O
);

  wire and_1_out, and_2_out, and_3_out, and_4_out, and_5_out, and_6_out, and_7_out, and_8_out;

  and and_1 (and_1_out, E, ~I[0]);  // AND_Gate
  and and_2 (and_2_out, E, I[0]);
  S_R_Flip_Flop #(.trigger("falling")) s_r_ff_1 (
    .S(and_2_out), .R(and_1_out), .clk(E), .Q(O[0]));  // open: reset, Qn, preset
  and and_3 (and_3_out, E, ~I[1]);  // AND_Gate
  and and_4 (and_4_out, E, I[1]);
  and and_5 (and_5_out, E, ~I[2]);  // AND_Gate
  and and_6 (and_6_out, E, I[2]);
  S_R_Flip_Flop #(.trigger("falling")) s_r_ff_2 (
    .S(and_4_out), .R(and_3_out), .clk(E), .Q(O[1]));  // open: reset, Qn, preset
  and and_7 (and_7_out, E, ~I[3]);  // AND_Gate
  and and_8 (and_8_out, E, I[3]);
  S_R_Flip_Flop #(.trigger("falling")) s_r_ff_3 (
    .S(and_6_out), .R(and_5_out), .clk(E), .Q(O[2]));  // open: reset, Qn, preset
  S_R_Flip_Flop #(.trigger("falling")) s_r_ff_4 (
    .S(and_8_out), .R(and_7_out), .clk(E), .Q(O[3]));  // open: reset, Qn, preset
endmodule

module PC_Circuit (
  input  [3:0] I,
  input  PC_Increment,
  input  PC_Load,
  input  PC_Write,
  output [3:0] O
);

  wire [3:0] incrementer_1_o, two_way_bus_mux_1_o;

  Incrementer incrementer_1 (.I(O), .O(incrementer_1_o));
  Two_Way_Bus_Mux two_way_bus_mux_1 (
    .I1(incrementer_1_o), .I2(I), .E1(PC_Increment), .E2(PC_Load), .O(two_way_bus_mux_1_o));
  PC_Register pc_register_1 (.I(two_way_bus_mux_1_o), .E(PC_Write), .O(O));
endmodule

module R_MUX_Three_Way (
  input  [7:0] ALU,
  input  [7:0] Mem,
  input  [3:0] IR,
  input  R_MUX_ALU,
  input  R_MUX_Mem,
  input  R_MUX_IR,
  output [7:0] O
);

  wire and_1_out, and_2_out, and_3_out, and_4_out, and_5_out, and_6_out, and_7_out, and_8_out, and_9_out,
       and_10_out, and_11_out, and_12_out, and_13_out, and_14_out, and_15_out, and_16_out, and_17_out,
       and_18_out, and_19_out, and_20_out, and_21_out, and_22_out, and_23_out, and_24_out;

  and and_1 (and_1_out, R_MUX_ALU, ALU[0]);
  and and_2 (and_2_out, R_MUX_Mem, Mem[0]);
  or or_1 (O[0], and_1_out, and_2_out, and_3_out);
  and and_3 (and_3_out, R_MUX_IR, IR[0]);
  and and_4 (and_4_out, R_MUX_ALU, ALU[1]);
  and and_5 (and_5_out, R_MUX_Mem, Mem[1]);
  or or_2 (O[1], and_4_out, and_5_out, and_6_out);
  and and_6 (and_6_out, R_MUX_IR, IR[1]);
  and and_7 (and_7_out, R_MUX_ALU, ALU[2]);
  and and_8 (and_8_out, R_MUX_Mem, Mem[2]);
  or or_3 (O[2], and_7_out, and_8_out, and_9_out);
  and and_9 (and_9_out, R_MUX_IR, IR[2]);
  and and_10 (and_10_out, R_MUX_ALU, ALU[3]);
  and and_11 (and_11_out, R_MUX_IR, IR[3]);
  and and_12 (and_12_out, R_MUX_Mem, Mem[3]);
  or or_4 (O[3], and_10_out, and_12_out, and_11_out);
  and and_13 (and_13_out, R_MUX_ALU, ALU[4]);
  and and_14 (and_14_out, R_MUX_Mem, Mem[4]);
  and and_15 (and_15_out, R_MUX_IR, 1'b0);
  or or_5 (O[4], and_13_out, and_14_out, and_15_out);
  and and_16 (and_16_out, R_MUX_ALU, ALU[5]);
  and and_17 (and_17_out, R_MUX_Mem, Mem[5]);
  and and_18 (and_18_out, R_MUX_IR, 1'b0);
  or or_6 (O[5], and_16_out, and_17_out, and_18_out);
  and and_19 (and_19_out, R_MUX_ALU, ALU[6]);
  and and_20 (and_20_out, R_MUX_Mem, Mem[6]);
  or or_7 (O[6], and_19_out, and_20_out, and_21_out);
  and and_21 (and_21_out, R_MUX_IR, 1'b0);
  and and_22 (and_22_out, R_MUX_ALU, ALU[7]);
  and and_23 (and_23_out, R_MUX_Mem, Mem[7]);
  or or_8 (O[7], and_22_out, and_23_out, and_24_out);
  and and_24 (and_24_out, R_MUX_IR, 1'b0);
endmodule

module Control_Circuit (
  input  Fetch,
  input  Fetch_Write,
  input  Execute,
  input  Execute_Write,
  input  [3:0] Opcode,
  input  [7:0] R,
  output Halt,
  output ALU_Add,
  output ALU_AND,
  output ALU_XOR,
  output Memory_Write,
  output ALU_LS,
  output ALU_RS,
  output PC_Increment,
  output R_MUX_ALU,
  output PC_Load,
  output R_MUX_Memory,
  output R_MUX_IR,
  output PC_Write,
  output ADDR_MUX_PC,
  output ADDR_MUX_IR,
  output R_Write,
  output IR_Write
);

  wire and_7_out, and_8_out, and_13_out, and_14_out, and_15_out, and_16_out, and_17_out, and_20_out,
       and_21_out, or_2_out, or_3_out, or_4_out;

  or or_1 (R_MUX_ALU, ALU_Add, ALU_LS, ALU_AND, ALU_RS, ALU_XOR);
  or or_2 (or_2_out, ALU_Add, ALU_AND, ALU_XOR);
  // AND_Gate and_1 has open pins: in0=Execute, in1=Opcode[1], in2=Opcode[0], in3=Opcode[2], in4=Opcode[3], out=open
  and and_2 (ALU_Add, Execute, Opcode[1], ~Opcode[0], ~Opcode[2], ~Opcode[3]);  // AND_Gate
  and and_3 (ALU_AND, Execute, ~Opcode[1], ~Opcode[0], Opcode[2], ~Opcode[3]);  // AND_Gate
  and and_4 (ALU_XOR, Execute, Opcode[1], ~Opcode[0], Opcode[2], ~Opcode[3]);  // AND_Gate
  and and_5 (R_MUX_IR, Execute, ~Opcode[1], ~Opcode[0], ~Opcode[2], Opcode[3]);  // AND_Gate
  and and_6 (R_MUX_Memory, Execute, Opcode[1], ~Opcode[0], ~Opcode[2], Opcode[3]);  // AND_Gate
  and and_7 (and_7_out, Execute, ~Opcode[1], ~Opcode[0], Opcode[2], Opcode[3]);  // AND_Gate
  and and_8 (and_8_out, Execute, Opcode[1], ~Opcode[0], Opcode[2], Opcode[3]);  // AND_Gate
  and and_9 (ALU_LS, Execute, Opcode[0], Opcode[1], ~Opcode[2], ~Opcode[3]);  // AND_Gate
  and and_10 (ALU_RS, Execute, Opcode[0], ~Opcode[1], Opcode[2], ~Opcode[3]);  // AND_Gate
  or or_3 (or_3_out, ALU_RS, ALU_LS, and_8_out);
  and and_11 (PC_Load, ~R[7], ~R[6], ~R[5], ~R[4], ~R[3], ~R[2], ~R[1], ~R[0], or_3_out);  // AND_Gate
  and and_12 (Halt, Execute_Write, ~Opcode[1], ~Opcode[0], ~Opcode[2], ~Opcode[3]);  // AND_Gate
  and and_13 (and_13_out, Execute_Write, Opcode[1], ~Opcode[0], ~Opcode[2], ~Opcode[3]);  // AND_Gate
  and and_14 (and_14_out, Execute_Write, ~Opcode[1], ~Opcode[0], Opcode[2], ~Opcode[3]);  // AND_Gate
  and and_15 (and_15_out, Execute_Write, Opcode[1], ~Opcode[0], Opcode[2], ~Opcode[3]);  // AND_Gate
  and and_16 (and_16_out, Execute_Write, ~Opcode[1], ~Opcode[0], ~Opcode[2], Opcode[3]);  // AND_Gate
  and and_17 (and_17_out, Execute_Write, Opcode[1], ~Opcode[0], ~Opcode[2], Opcode[3]);  // AND_Gate
  and and_18 (Memory_Write, Execute_Write, ~Opcode[1], ~Opcode[0], Opcode[2], Opcode[3]);  // AND_Gate
  // AND_Gate and_19 has open pins: in0=Execute_Write, in1=Opcode[1], in2=Opcode[0], in3=Opcode[2], in4=Opcode[3], out=open
  and and_20 (and_20_out, Execute_Write, Opcode[0], Opcode[1], ~Opcode[2], ~Opcode[3]);  // AND_Gate
  and and_21 (and_21_out, Execute_Write, Opcode[0], ~Opcode[1], Opcode[2], ~Opcode[3]);  // AND_Gate
  or or_4 (or_4_out, and_17_out, and_16_out, and_15_out, and_14_out, and_13_out);
  or or_5 (R_Write, and_21_out, and_20_out, or_4_out);
  not not_1 (PC_Increment, PC_Load);
  or or_6 (ADDR_MUX_IR, and_7_out, or_2_out, R_MUX_Memory);

  assign ADDR_MUX_PC = Fetch;
  assign IR_Write = Fetch_Write;
  assign PC_Write = Execute_Write;
endmodule
